// Digital circuit Lab1Schematic.dig as structural Verilog
module Lab1Schematic (
  input  A,
  input  B,
  input  C,
  input  D,
  output Y
);

  wire _7404_1_pin3, _7404_1_pin5, _7404_1_pin9, _7404_1_pin11, _7404_1_pin13, _74151_1_pin12;

  _74151 _74151_1 (
    .pin1(A), .pin2(A), .pin3(A), .pin4(A), .pin5(Y), .pin7(1'b0), .pin8(1'b0), .pin9(D), .pin10(C),
    .pin11(B), .pin12(_74151_1_pin12), .pin13(_74151_1_pin12), .pin14(_74151_1_pin12),
    .pin15(_74151_1_pin12), .pin16(1'b1));  // open: pin6
  _7404 _7404_1 (
    .pin1(A), .pin2(_74151_1_pin12), .pin3(_7404_1_pin3), .pin5(_7404_1_pin5), .pin7(1'b0),
    .pin9(_7404_1_pin9), .pin11(_7404_1_pin11), .pin13(_7404_1_pin13), .pin14(1'b1));  // open: pin4, pin6, pin8, pin10, pin12
  // NotConnected on _7404_1_pin3
  // NotConnected on _7404_1_pin5
  // NotConnected on _7404_1_pin13
  // NotConnected on _7404_1_pin11
  // NotConnected on _7404_1_pin9
endmodule

/* Test case:
D C B A Y
0 0 0 1 1
0 0 1 0 0
0 0 1 1 1
0 1 0 0 0
0 1 0 1 1
0 1 1 0 0
0 1 1 1 1
1 0 0 0 1
1 0 0 1 0
1 0 1 0 1
1 0 1 1 0
1 1 0 0 1
*/
